# Fritzing sketch PhotodiodeSetup (saved by Fritzing 0.9.3b)
circuit board: 3.2cm x 3.2cm
breadboards: 1

parts:
  X1 = DB9 Connector [package=db9]
  IC5 = Voltage Regulator [package=to-220-alt]
  IC4 = Voltage Regulator [package=to-220-alt]
  IC3 = Voltage Regulator [package=to-220-alt]
  IC2 = Voltage Regulator [package=to-220-alt]

nets:
  GND: X1.1, IC5.GND, IC4.GND, IC3.GND, IC2.GND
  N1: X1.2, IC5.IN, IC4.IN, IC3.IN, IC2.IN
  N2: X1.5, IC5.OUT
  N3: X1.6, IC3.OUT
  N4: X1.7, IC4.OUT
  N5: X1.8, IC2.OUT

notes:
  TSL250R
  GND, Vdd, Out
