# Fritzing sketch VRLate (saved by Fritzing 0.9.3b)
breadboards: 2

parts:
  Teensy_3_1 = Teensy 3.1  # not connected
  Bauteil1 = FTDI Basic Programmer
  J5 = female pin header, 5 pins [form="♀ (female)"]
  LED1 = LED - 5mm [color="Yellow (595nm)" package="5 mm [THT]"]
  R1 = Resistor [tolerance=±5% resistance=220 package=THT]
  VCC1 = 4 x AAA Battery Mount
  J6 = Basic Servo
  R2 = Rotary Potentiometer (Large) [maximum_resistance=50kΩ package=THT]
  X2 = DB9 Connector [package=db9]
  TRRS1 = Audio Jack (TRRS) 3.5mm [part_number="LUMBERG JEITA RC-5325A" package="RC-5325A [SMD]"]
  TRRS2 = Audio Jack (TRRS) 3.5mm [part_number="LUMBERG JEITA RC-5325A" package="RC-5325A [SMD]"]
  LED2 = LED - 5mm [color="Red (635nm)" package="5 mm [THT]"]
  R3 = Resistor [tolerance=±5% resistance=220 package=THT]
  VCC2 = 4 x AAA Battery Mount
  J7 = Piezo Speaker
  R4 = Resistor [tolerance=±5% resistance=330 package=THT]
  JP1 = Header 4 [package=screwterminal-3.5mm-4_lock]

nets:
  GND: Bauteil1.GND, R1.Pin_0, VCC1.-, J6.gnd, TRRS2.SLEEVE, R3.Pin_0, J7.pin1, JP1.2
  N1: J5.pin1, TRRS1.TIP
  N2: J5.pin3, TRRS1.RING1
  N3: J5.pin4, TRRS1.SLEEVE, VCC2.-
  N4: J5.pin5, VCC2.+
  N5: LED1.cathode, R1.Pin_1
  N6: VCC1.+, J6.vcc, JP1.3
  N7: R2.leg1, X2.1
  N8: R2.leg2, X2.2
  N9: LED2.cathode, R3.Pin_1
  N10: J7.pin2, R4.Pin_0

notes:
  GPS - Ublox - NEO 6m
  PPS - RXD - TXD - GND - VCC
  Photosensor
  Status LEDs:
  Red: Measureing
  Yellow: GPS Fix
  31072-MP:
  AO Gnd Vcc DO
